# Fritzing sketch TestCircuitSketch (saved by Fritzing 0.9.4)

parts:
  Part1 = Arduino XBee Shield
  U1 = XBEE-1 [package=xbee-1_lock]  # not connected
  Part2 = Arduino Uno (Rev3)  # not connected
  microSD1 = MicroSD Card Module

nets:
  5V: Part1.5V, microSD1.VCC
  N1: Part1.D4, microSD1.CS
  N2: Part1.D11, microSD1.MOSI
  N3: Part1.D12, microSD1.MISO
  N4: Part1.D13, microSD1.SCK
  GND: Part1.GND, microSD1.GND
